// Logisim project CHAMPS-TTL.circ as structural Verilog: 7 circuits, main circuit CHAMPS-TTL
module CHAMPS_TTL (
);

  wire ACC, address_register_4_bits_1_q5, clk, F0, F1, F2, F3, JMP, M, MW, nand_1_out, Z;
  wire [3:0] accumulator_register_4_bits_1_q, address_register_4_bits_1_q, alu_1_alu,
       mux_2_1_4_bits_1_output, program_counter_4_bits_1_outputs, ram_1_data;
  wire [7:0] rom_1_data;

  Clock_part clock_1 (.out(clk));
  nand nand_1 (nand_1_out, JMP, Z);
  Hex_Digit_Display hex_digit_display_1 (.value(program_counter_4_bits_1_outputs));  // open: dp
  Program_Counter__4_bits program_counter_4_bits_1 (
    .CP(clk), .nLD(nand_1_out), .Outputs(program_counter_4_bits_1_outputs), .Inputs(mux_2_1_4_bits_1_output));
  Hex_Digit_Display hex_digit_display_2 (.value(mux_2_1_4_bits_1_output));  // open: dp
  Address_Register__4_bits address_register_4_bits_1 (
    .CP(clk), .D(mux_2_1_4_bits_1_output), .D5(MW), .Q5(address_register_4_bits_1_q5),
    .Q(address_register_4_bits_1_q));
  Hex_Digit_Display hex_digit_display_3 (.value(address_register_4_bits_1_q));  // open: dp
  Hex_Digit_Display hex_digit_display_4 (.value(accumulator_register_4_bits_1_q));  // open: dp
  ROM #(.addrWidth(4)) rom_1 (.addr(program_counter_4_bits_1_outputs), .data(rom_1_data));  // open: sel
  ROM #(.addrWidth(3)) rom_2 (.addr(rom_1_data[7:5]), .data({M, F3, F2, F1, F0, ACC, MW, JMP}));  // open: sel
  Hex_Digit_Display hex_digit_display_5 (.value(rom_1_data[3:0]));  // open: dp
  Mux_2_1__4_bits mux_2_1_4_bits_1 (
    .Input_0(rom_1_data[3:0]), .Input_1(ram_1_data), .Output(mux_2_1_4_bits_1_output), .Select(rom_1_data[4]));
  ALU alu_1 (
    .AC(accumulator_register_4_bits_1_q), .Bus(mux_2_1_4_bits_1_output), .ALU(alu_1_alu), .A_B(Z), .M(M),
    .Cn(F0), .S({F3, F2, F1, F0}));  // open: Carry
  Hex_Digit_Display hex_digit_display_6 (.value(alu_1_alu));  // open: dp
  Accumulator_Register__4_bits accumulator_register_4_bits_1 (
    .nE(ACC), .CP(clk), .D(alu_1_alu), .Q(accumulator_register_4_bits_1_q));
  Hex_Digit_Display hex_digit_display_7 (.value(ram_1_data));  // open: dp
  RAM #(.addrWidth(4), .dataWidth(4), .bus("separate")) ram_1 (
    .addr(address_register_4_bits_1_q), .din(accumulator_register_4_bits_1_q), .data(ram_1_data),
    .str(address_register_4_bits_1_q5), .clk(clk), .ld(1'b1));  // open: sel, clr

  // Notes on the sheet:
  //   PGM ROM
  //   CU ROM
  //   contents of rom_1 (hex, n*v repeats v):
  //   80 10 81 30 6f 8f 90 10 61 80 10 41 60 cd a0
  //   contents of rom_2 (hex, n*v repeats v):
  //   d0 48 30 6 4 e5 85
endmodule

// Mux 2-1
module Mux_2_1__4_bits (
  input  Select,
  input  [3:0] Input_0,
  input  [3:0] Input_1,
  output [3:0] Output
);

  _74157 u_74157_1 (
    ._1__S(Select), ._2__A1(Input_0[0]), ._3__B1(Input_1[0]), ._4__Y1(Output[0]), ._5__A2(Input_0[1]),
    ._6__B2(Input_1[1]), ._7__Y2(Output[1]), ._15__G(1'b0), ._14__A4(Input_0[3]), ._13__B4(Input_1[3]),
    ._12__Y4(Output[3]), ._11__A3(Input_0[2]), ._10__B3(Input_1[2]), ._9__Y3(Output[2]));  // open: _8__GND, _16__Vcc
endmodule

module ALU (
  input  M,
  input  Cn,
  input  [3:0] S,
  input  [3:0] AC,
  input  [3:0] Bus,
  output [3:0] ALU,
  output A_B,
  output Carry
);

  _74181 u_74181_1 (
    ._1__nB0(Bus[0]), ._2__nA0(AC[0]), ._3__S3(S[3]), ._4__S2(S[2]), ._5__S1(S[1]), ._6__S0(S[0]),
    ._7__Cn(Cn), ._8__M(M), ._9__nF0(ALU[0]), ._10__nF1(ALU[1]), ._11__nF2(ALU[2]), ._23__nA1(AC[1]),
    ._22__nB1(Bus[1]), ._21__nA2(AC[2]), ._20__nB2(Bus[2]), ._19__nA3(AC[3]), ._18__nB3(Bus[3]),
    ._16__Cn_4(Carry), ._14__A_B(A_B), ._13__nF3(ALU[3]));  // open: _12__GND, _24__Vcc, _17__nG, _15__nP
endmodule

// Accumulator
module Accumulator_Register__4_bits (
  input  [3:0] D,
  input  nE,
  input  CP,
  output [3:0] Q
);

  _74377 u_74377_1 (
    ._1__nE(nE), ._2__Q0(Q[0]), ._3__D0(D[0]), ._4__D1(D[1]), ._5__Q1(Q[1]), ._6__Q2(Q[2]), ._7__D2(D[2]),
    ._8__D3(D[3]), ._9__Q3(Q[3]), ._11__CP(CP));  // open: _10__GND, _20__Vcc, _19__Q7, _18__D7, _17__D6, _16__Q6, _15__Q5, _14__D5, _13__D4, _12__Q4
endmodule

// Address
module Address_Register__4_bits (
  input  [3:0] D,
  input  D5,
  input  CP,
  output Q5,
  output [3:0] Q
);

  _74174 u_74174_1 (
    ._1__MR_prime(1'b1), ._2__Q0(Q[0]), ._3__D0(D[0]), ._4__D1(D[1]), ._5__Q1(Q[1]), ._6__D2(D[2]),
    ._7__Q2(Q[2]), ._15__Q5(Q5), ._14__D5(D5), ._11__D3(D[3]), ._10__Q3(Q[3]), ._9__CP(CP));  // open: _8__GND, _16__Vcc, _13__D4, _12__Q4
endmodule

// PC
module Program_Counter__4_bits (
  input  CP,
  input  nLD,
  input  [3:0] Inputs,
  output [3:0] Outputs
);

  _74161 u_74161_1 (
    ._1__nMR(1'b1), ._2__CP(CP), ._3__D0(Inputs[0]), ._4__D1(Inputs[1]), ._5__D2(Inputs[2]),
    ._6__D3(Inputs[3]), ._7__CEP(1'b1), ._14__Q0(Outputs[0]), ._13__Q1(Outputs[1]), ._12__Q2(Outputs[2]),
    ._11__O3(Outputs[3]), ._10__CET(1'b1), ._9__nPE(nLD));  // open: _8__GND, _16__Vcc, _15__TC
endmodule

module Clock (
  output Q,
  output nQ
);

  wire pull_resistor_1_node, pull_resistor_2_node;

  Pull_Resistor #(.pull(1)) pull_resistor_1 (.node(pull_resistor_1_node));
  Pull_Resistor #(.pull(1)) pull_resistor_2 (.node(pull_resistor_2_node));
  nand nand_1 (Q, pull_resistor_1_node, nQ);
  nand nand_2 (nQ, Q, pull_resistor_2_node);

  // Notes on the sheet:
  //   /S
  //   /R
endmodule
