// Logisim project CHAMPS.circ as structural Verilog: 11 circuits, main circuit CHAMPS
module CHAMPS (
);

  wire ACC, address_register_4_bits_1_q5, and_1_out, clk, F0, F1, F2, JMP, MW, Z;
  wire [3:0] accumulator_register_4_bits_1_q, address_register_4_bits_1_q, alu_1_alu,
       mux_2_1_4_bits_1_output, program_counter_4_bits_1_outputs, ram_1_data;
  wire [7:0] rom_1_data;

  Clock_part clock_1 (.out(clk));
  and and_1 (and_1_out, JMP, Z);
  Hex_Digit_Display hex_digit_display_1 (.value(program_counter_4_bits_1_outputs));  // open: dp
  Hex_Digit_Display hex_digit_display_2 (.value(mux_2_1_4_bits_1_output));  // open: dp
  Hex_Digit_Display hex_digit_display_3 (.value(address_register_4_bits_1_q));  // open: dp
  Program_Counter__4_bits program_counter_4_bits_1 (
    .clk(clk), .nLD(and_1_out), .Inputs(mux_2_1_4_bits_1_output), .Outputs(program_counter_4_bits_1_outputs));
  Address_Register__4_bits address_register_4_bits_1 (
    .clk(clk), .D(mux_2_1_4_bits_1_output), .D5(MW), .Q5(address_register_4_bits_1_q5),
    .Q(address_register_4_bits_1_q));
  Hex_Digit_Display hex_digit_display_4 (.value(accumulator_register_4_bits_1_q));  // open: dp
  ROM #(.addrWidth(4)) rom_1 (.addr(program_counter_4_bits_1_outputs), .data(rom_1_data));  // open: sel
  ROM #(.addrWidth(3), .dataWidth(6)) rom_2 (.addr(rom_1_data[7:5]), .data({F2, F1, F0, ACC, MW, JMP}));  // open: sel
  ALU alu_1 (
    .Functions({F2, F1, F0}), .AC(accumulator_register_4_bits_1_q), .Bus(mux_2_1_4_bits_1_output),
    .ALU(alu_1_alu), .Z(Z));  // open: Carry
  Accumulator_Register__4_bits accumulator_register_4_bits_1 (
    .W(ACC), .clk(clk), .D(alu_1_alu), .Q(accumulator_register_4_bits_1_q));
  Hex_Digit_Display hex_digit_display_5 (.value(rom_1_data[3:0]));  // open: dp
  Hex_Digit_Display hex_digit_display_6 (.value(ram_1_data));  // open: dp
  Mux_2_1__4_bits mux_2_1_4_bits_1 (
    .Input_0(rom_1_data[3:0]), .Input_1(ram_1_data), .Output(mux_2_1_4_bits_1_output), .Select(rom_1_data[4]));
  Hex_Digit_Display hex_digit_display_7 (.value(alu_1_alu));  // open: dp
  RAM #(.addrWidth(4), .dataWidth(4), .bus("separate")) ram_1 (
    .addr(address_register_4_bits_1_q), .din(accumulator_register_4_bits_1_q), .data(ram_1_data),
    .str(address_register_4_bits_1_q5), .clk(clk), .ld(1'b1));  // open: sel, clr

  // Notes on the sheet:
  //   PGM ROM
  //   CU ROM
  //   contents of rom_1 (hex, n*v repeats v):
  //   80 10 81 30 6f 8f 90 10 61 80 10 41 60 cd a0
  //   contents of rom_2 (hex, n*v repeats v):
  //   1c 4 c 2 0 21 11
endmodule

// Mux 2-1
module Mux_2_1__4_bits (
  input  Select,
  input  [3:0] Input_0,
  input  [3:0] Input_1,
  output [3:0] Output
);

  Mux_2_1 mux_2_1_1 (.Input_0(Input_0[0]), .Input_1(Input_1[0]), .Output(Output[0]), .Select(Select));
  Mux_2_1 mux_2_1_2 (.Input_0(Input_0[1]), .Input_1(Input_1[1]), .Output(Output[1]), .Select(Select));
  Mux_2_1 mux_2_1_3 (.Input_0(Input_0[2]), .Input_1(Input_1[2]), .Output(Output[2]), .Select(Select));
  Mux_2_1 mux_2_1_4 (.Input_0(Input_0[3]), .Input_1(Input_1[3]), .Output(Output[3]), .Select(Select));
endmodule

module ALU (
  input  [2:0] Functions,
  input  [3:0] AC,
  input  [3:0] Bus,
  output [3:0] ALU,
  output Z,
  output Carry
);

  wire [3:0] adder_4_bits_1_p5, xor_1_out;

  assign xor_1_out = {4{Functions[0]}} ^ Bus;  // XOR_Gate xor_1, 4 bits wide
  // Processeur_Adder_4_bits adder_4_bits_1: pin names not known; wires that end beside it: AC, xor_1_out, Functions[0], Carry, adder_4_bits_1_p5
  Mux_8_1__4_bits mux_8_1_4_bits_1 (
    .Output(ALU), .Select_0(Functions[0]), .Select_1(Functions[1]), .Select_2(Functions[2]),
    .Input_0(adder_4_bits_1_p5), .Input_7(4'b0000), .Input_1(adder_4_bits_1_p5), .Input_6(4'b0000),
    .Input_2(AC), .Input_5(4'b0000), .Input_3(Bus), .Input_4(4'b0000));
  nor nor_1 (Z, ALU[0], ALU[1], ALU[2], ALU[3]);
endmodule

// Accumulator
module Accumulator_Register__4_bits (
  input  W,
  input  clk,
  input  [3:0] D,
  output [3:0] Q
);

  D_Flip_Flop d_ff_1 (.clk(clk), .D(D[0]), .Q(Q[0]), .en(W));  // open: Qn, preset, reset
  D_Flip_Flop d_ff_2 (.clk(clk), .D(D[1]), .Q(Q[1]), .en(W));  // open: Qn, preset, reset
  D_Flip_Flop d_ff_3 (.clk(clk), .D(D[2]), .Q(Q[2]), .en(W));  // open: Qn, preset, reset
  D_Flip_Flop d_ff_4 (.clk(clk), .D(D[3]), .Q(Q[3]), .en(W));  // open: Qn, preset, reset
endmodule

// Address
module Address_Register__4_bits (
  input  D5,
  input  [3:0] D,
  input  clk,
  output Q5,
  output [3:0] Q
);

  D_Flip_Flop d_ff_1 (.clk(clk), .D(D[0]), .Q(Q[0]));  // open: Qn, preset, en, reset
  D_Flip_Flop d_ff_2 (.clk(clk), .D(D[1]), .Q(Q[1]));  // open: Qn, preset, en, reset
  D_Flip_Flop d_ff_3 (.clk(clk), .D(D[2]), .Q(Q[2]));  // open: Qn, preset, en, reset
  D_Flip_Flop d_ff_4 (.clk(clk), .D(D[3]), .Q(Q[3]));  // open: Qn, preset, en, reset
  D_Flip_Flop d_ff_5 (.clk(clk), .D(D5), .Q(Q5));  // open: Qn, preset, en, reset
endmodule

// PC
module Program_Counter__4_bits (
  input  nLD,
  input  clk,
  input  [3:0] Inputs,
  output [3:0] Outputs
);

  wire not_1_out;

  Counter #(.width(4), .max('hf)) counter_1 (
    .load(nLD), .D(Inputs), .count(not_1_out), .Q(Outputs), .clk(clk));  // open: carry, clr
  not not_1 (not_1_out, nLD);
endmodule

module Clock (
  output Q,
  output nQ
);

  wire pull_resistor_1_node, pull_resistor_2_node;

  Pull_Resistor #(.pull(1)) pull_resistor_1 (.node(pull_resistor_1_node));
  Pull_Resistor #(.pull(1)) pull_resistor_2 (.node(pull_resistor_2_node));
  nand nand_1 (Q, pull_resistor_1_node, nQ);
  nand nand_2 (nQ, Q, pull_resistor_2_node);

  // Notes on the sheet:
  //   /S
  //   /R
endmodule

module Mux_2_1 (
  input  Select,
  input  Input_0,
  input  Input_1,
  output Output
);

  wire and_1_out, and_2_out, not_1_out;

  not not_1 (not_1_out, Select);
  and and_1 (and_1_out, not_1_out, Input_0);
  and and_2 (and_2_out, Select, Input_1);
  or or_1 (Output, and_1_out, and_2_out);
endmodule

module Adder_4_bits (
  input  Cin,
  input  [3:0] A,
  input  [3:0] B,
  output [3:0] Sum,
  output overflow,
  output Cout
);

  wire fulladder_1_cout, fulladder_2_cout, fulladder_3_cout;

  FullAdder fulladder_1 (.A(A[0]), .B(B[0]), .S(Sum[0]), .Cin(Cin), .Cout(fulladder_1_cout));
  FullAdder fulladder_2 (.A(A[1]), .B(B[1]), .S(Sum[1]), .Cin(fulladder_1_cout), .Cout(fulladder_2_cout));
  FullAdder fulladder_3 (.A(A[2]), .B(B[2]), .S(Sum[2]), .Cin(fulladder_2_cout), .Cout(fulladder_3_cout));
  FullAdder fulladder_4 (.A(A[3]), .B(B[3]), .S(Sum[3]), .Cin(fulladder_3_cout), .Cout(Cout));
  xor xor_1 (overflow, fulladder_3_cout, Cout);
endmodule

module FullAdder (
  input  Cin,
  input  A,
  input  B,
  output S,
  output Cout
);

  wire and_1_out, and_2_out, and_3_out;

  xor xor_1 (S, A, B, Cin);
  and and_1 (and_1_out, A, B);
  and and_2 (and_2_out, A, Cin);
  and and_3 (and_3_out, B, Cin);
  or or_1 (Cout, and_1_out, and_2_out, and_3_out);
endmodule

// Mux 8-1
module Mux_8_1__4_bits (
  input  Select_0,
  input  Select_1,
  input  Select_2,
  input  [3:0] Input_7,
  input  [3:0] Input_6,
  input  [3:0] Input_5,
  input  [3:0] Input_4,
  input  [3:0] Input_3,
  input  [3:0] Input_2,
  input  [3:0] Input_1,
  input  [3:0] Input_0,
  output [3:0] Output
);

  wire [3:0] mux_2_1_4_bits_1_output, mux_2_1_4_bits_2_output, mux_2_1_4_bits_3_output,
       mux_2_1_4_bits_4_output, mux_2_1_4_bits_5_output, mux_2_1_4_bits_6_output;

  Mux_2_1__4_bits mux_2_1_4_bits_1 (
    .Input_0(Input_6), .Input_1(Input_7), .Output(mux_2_1_4_bits_1_output), .Select(Select_0));
  Mux_2_1__4_bits mux_2_1_4_bits_2 (
    .Input_0(Input_4), .Input_1(Input_5), .Output(mux_2_1_4_bits_2_output), .Select(Select_0));
  Mux_2_1__4_bits mux_2_1_4_bits_3 (
    .Input_0(Input_2), .Input_1(Input_3), .Output(mux_2_1_4_bits_3_output), .Select(Select_0));
  Mux_2_1__4_bits mux_2_1_4_bits_4 (
    .Input_0(Input_0), .Input_1(Input_1), .Output(mux_2_1_4_bits_4_output), .Select(Select_0));
  Mux_2_1__4_bits mux_2_1_4_bits_5 (
    .Input_0(mux_2_1_4_bits_2_output), .Input_1(mux_2_1_4_bits_1_output), .Output(mux_2_1_4_bits_5_output),
    .Select(Select_1));
  Mux_2_1__4_bits mux_2_1_4_bits_6 (
    .Input_0(mux_2_1_4_bits_4_output), .Input_1(mux_2_1_4_bits_3_output), .Output(mux_2_1_4_bits_6_output),
    .Select(Select_1));
  Mux_2_1__4_bits mux_2_1_4_bits_7 (
    .Input_0(mux_2_1_4_bits_6_output), .Input_1(mux_2_1_4_bits_5_output), .Output(Output), .Select(Select_2));
endmodule
